# Fritzing sketch door (saved by Fritzing 1.0.1rc)
breadboards: 2

parts:
  Part1 = Arduino Mega 2560 (Rev3)
  IR1 = TSOP312.., 314.. [package=THT]
  M1 = Dagu DGServo 9g (Pan and tilt) [part_number=RS001B]
  LCD1 = LCD screen
  Mod1 = Passive Buzzer
  LED1 = smd LED [color="Red (633nm)" package="0603 [SMD]"]
  R1 = Resistor [tolerance=±5% power=0.25 resistance=220 package=THT]
  R2 = Trimmer Potentiometer [maximum_resistance=10kΩ knob_status=50% package=THT]  # not connected
  Part2 = RFID-RC522-v2
  Part3 = 4x4 Keypad [part_number=101207]

nets:
  N1: Part1.D18/TX1, IR1.Data
  GND: Part1.GND, M1.gnd, LCD1.VSS, LCD1.LED-, R1.Pin_1, Part2.GND
  N2: Part1.D11_PWM, LED1.anode
  N3: Part1.D10_PWM, Mod1.S
  N4: Part1.D9_PWM, M1.pulse
  3V3: Part1.3V3, Part2.3.3V
  N5: Part1.D5_PWM, Part2.RST
  5V: Part1.5V, M1.vcc, LCD1.VDD, LCD1.LED+
  N6: Part1.D30, Part3.1
  N7: Part1.D31, Part3.2
  N8: Part1.D32, Part3.3
  N9: Part1.D33, Part3.4
  N10: Part1.D34, Part3.5
  N11: Part1.D35, Part3.6
  N12: Part1.D36, Part3.7
  N13: Part1.D37, Part3.8
  N14: Part1.D38, LCD1.RS
  N15: Part1.D39, LCD1.E
  N16: Part1.D40, LCD1.DB4
  N17: Part1.D41, LCD1.DB5
  N18: Part1.D42, LCD1.DB6
  N19: Part1.D43, LCD1.DB7
  N20: Part1.D50, Part2.MISO
  N21: Part1.D51, Part2.MOSI
  N22: Part1.D52, Part2.SCK
  N23: Part1.D53, Part2.SDA
  N24: IR1.GND, Mod1.-
  N25: IR1.Vs, Mod1.NC
  N26: LED1.cathode, R1.Pin_0

custom parts:
  RFID-RC522-v2: A simple China made RFID-RC522 Reader; do check the pin labels, as this is a MFRC522 based clone.
  4x4 Keypad: Matrix membrane keypad 4x4
