# Fritzing sketch radar (saved by Fritzing 1.0.1rc)
breadboards: 1

parts:
  Part1 = Arduino Uno (Rev3) - ICSP
  J1 = Basic Servo
  HC-SR04_Sensor_1 = HC-SR04 Ultrasonic Distance Sensor
  SG1 = Buzzer 12mm [package=buzzer-ccv-kit]
  LED1 = smd LED [color="Red (633nm)" package="0603 [SMD]"]
  R1 = Resistor [tolerance=±5% resistance=220 package="0805 [SMD]"]
  LCD1 = LCD screen
  R2 = TRIMPOT [knob_status=50% package=trimpot-5mm]

nets:
  N1: Part1.A5/SCL, LED1.anode
  VCC: Part1.5V, J1.vcc, HC-SR04_Sensor_1.VCC, LCD1.LED+, R2.CCW
  GND: Part1.GND, J1.gnd, HC-SR04_Sensor_1.GND, SG1.2, R1.Pin_1, LCD1.VSS, LCD1.R/W, LCD1.LED-, R2.WIPER
  N2: Part1.D8, SG1.1
  N3: Part1.D9_PWM, J1.pulse
  N4: Part1.D10_PWM/SS, HC-SR04_Sensor_1.TRIG
  N5: Part1.D11_PWM/MOSI, HC-SR04_Sensor_1.ECHO
  N6: Part1.D2, LCD1.RS
  N7: Part1.D3_PWM, LCD1.E
  N8: Part1.D4, LCD1.DB4
  N9: Part1.D5_PWM, LCD1.DB5
  N10: Part1.D6_PWM, LCD1.DB6
  N11: Part1.D7, LCD1.DB7
  N12: LCD1.V0, R2.CW
