# Fritzing sketch speed (saved by Fritzing 1.0.1rc)
breadboards: 1

parts:
  HC-SR04_Sensor_1 = HC-SR04 Ultrasonic Distance Sensor
  HC-SR04_Sensor_2 = HC-SR04 Ultrasonic Distance Sensor
  Nano1 = Arduino Nano v2.3
  LCD1 = LCD screen
  R1 = TRIMPOT [knob_status=50% package=trimpot_tc33]
  LED1 = smd LED [color="Red (633nm)" package="0603 [SMD]"]
  R2 = Resistor [tolerance=±5% resistance=220 package="0805 [SMD]"]
  SG1 = Buzzer 12mm [package=buzzer-ccv-kit]

nets:
  VCC: HC-SR04_Sensor_1.VCC, HC-SR04_Sensor_2.VCC, Nano1.+5V, LCD1.VDD, LCD1.LED+, R1.WIPER
  N1: HC-SR04_Sensor_1.TRIG, Nano1.D4
  N2: HC-SR04_Sensor_1.ECHO, Nano1.D5
  GND: HC-SR04_Sensor_1.GND, HC-SR04_Sensor_2.GND, Nano1.GND, LCD1.VSS, LCD1.R/W, LCD1.LED-, R1.CCW, R2.Pin_0, SG1.2
  N3: HC-SR04_Sensor_2.TRIG, Nano1.D2
  N4: HC-SR04_Sensor_2.ECHO, Nano1.D3
  N5: Nano1.D7, LCD1.RS
  N6: Nano1.D8, LCD1.E
  N7: Nano1.D9, LCD1.DB4
  N8: Nano1.D10, LCD1.DB5
  N9: Nano1.D11, LCD1.DB6
  N10: Nano1.D12, LCD1.DB7
  N11: Nano1.A1, LED1.anode
  N12: Nano1.A0, SG1.1
  N13: LCD1.V0, R1.CW
  N14: LED1.cathode, R2.Pin_1
